# Fritzing sketch piano (saved by Fritzing 0.9.4)
breadboards: 1

parts:
  R1 = Resistor [tolerance=±5% resistance=220 package=THT]
  R2 = Resistor [tolerance=±5% resistance=330 package=THT]
  R3 = Resistor [tolerance=±5% resistance=470 package=THT]
  LED1 = RGB LED (com. cathode, rgb) [package="5 mm [THT]"]
  Raspberry_Pi_A1 = Raspberry Pi A
  HC-SR04_Sensor_1 = HC-SR04 Ultrasonic Distance Sensor
  R4 = Resistor [tolerance=±5% resistance=220 package="1206 [SMD]"]
  R5 = Resistor [tolerance=±5% resistance=220 package="1206 [SMD]"]

nets:
  N1: R1.Pin_0, Raspberry_Pi_A1.GPIO_17
  N2: R1.Pin_1, LED1.red_anode
  N3: R2.Pin_0, R3.Pin_1, Raspberry_Pi_A1.GPIO_24
  N4: R2.Pin_1, HC-SR04_Sensor_1.ECHO
  GND: R3.Pin_0, LED1.common_cathode, Raspberry_Pi_A1.GND, HC-SR04_Sensor_1.GND
  N5: LED1.green_anode, R5.Pin_1
  N6: LED1.blue_anode, R4.Pin_1
  5V: Raspberry_Pi_A1.5V, HC-SR04_Sensor_1.VCC
  N7: Raspberry_Pi_A1.GPIO_18, HC-SR04_Sensor_1.TRIG
  N8: Raspberry_Pi_A1.GPIO_27, R5.Pin_0
  N9: Raspberry_Pi_A1.GPIO_22, R4.Pin_0

notes:
  USB1 to USB B port of touchscreen
  HDMI to HDMI port of touchscreen
  USB C to power source
